# Fritzing sketch frighino (saved by Fritzing 0.9.3b)
breadboards: 1

parts:
  Componente1 = Arduino Uno (Rev3)  # not connected
  T1 = LM35 Temperature Sensor [package="TO92 [THT]"]
  T2 = LM35 Temperature Sensor [package="TO92 [THT]"]
  T3 = LM35 Temperature Sensor [package="TO92 [THT]"]
  T4 = LM35 Temperature Sensor [package="TO92 [THT]"]
  R2 = Resistor [tolerance=±5% resistance=220 package="2512 [SMD]"]
  R3 = Resistor [tolerance=±5% resistance=220 package="2512 [SMD]"]
  R4 = Resistor [tolerance=±5% resistance=220 package="2512 [SMD]"]
  Q1 = MOSFET-NCHANNEL [package=to220v]  # not connected
  Q2 = MOSFET-NCHANNEL [package=to220v]  # not connected
  Q3 = MOSFET-NCHANNEL [package=to220v]  # not connected
  U1 = RELAY [package=relay-t9a]  # not connected
  R1 = Resistor [tolerance=±5% resistance=220 package="2512 [SMD]"]

nets:
  GND: T1.GND, T2.GND, T3.GND, T4.GND, R2.Pin_0
  N1: R3.Pin_0, R4.Pin_1, R1.Pin_0
